# Fritzing sketch powerACS712 (saved by Fritzing 0.9.3b)

parts:
  WeMos_D1_Mini1 = WeMos D1 Mini
  U1 = PCF8574 [package="DIP16 [THT]"]
  U2 = LCD-16X2 [package=lcd-16x2_noholes]
  U3 = ACS712 [package=so08]
  R1 = Slide Potentiometer [maximum_resistance=10kΩ]
  R2 = Resistor [tolerance=±20% resistance=1k package=THT]
  R3 = Resistor [tolerance=±20% resistance=1k package=THT]
  M1 = DC Motor
  VCC1 = Battery block 9V
  U4 = RELAY [package=relay-t9a-2]
  U5 = Sharp PC817 [package=THT]
  R4 = Resistor [tolerance=±5% resistance=1k package=THT]
  R5 = Resistor [tolerance=±5% resistance=1k package=THT]
  Q1 = NPN-Transistor [package="TO92 [THT]"]
  D1 = Rectifier Diode [part_number=1N4001 package="300 mil [THT]"]
  LED1 = LED - 5mm [color="Red (633nm)" package="5 mm [THT]"]
  R6 = Resistor [tolerance=±5% resistance=220 package=THT]

nets:
  5V: WeMos_D1_Mini1.5V, U1.VCC, U2.VDD, U2.A, U3.VCC, R1.leg2, U4.COIL1, U5.Pin_4, R4.Pin_0, D1.cathode
  Current: WeMos_D1_Mini1.A0, R2.Pin_1, R3.Pin_1
  SCL: WeMos_D1_Mini1.D1, U1.SCL
  SDA: WeMos_D1_Mini1.D2, U1.SDA
  LOAD: WeMos_D1_Mini1.D3, U5.Pin_2
  STATUS: WeMos_D1_Mini1.D4, R6.Pin_0
  GND: WeMos_D1_Mini1.G, U1.A0, U1.A1, U1.A3, U1.GND, U2.VSS, U2.K, U3.GND, R1.leg1, R3.Pin_0, Q1.E, LED1.cathode
  RS: U1.P0, U2.RS
  RW: U1.P1, U2.R_W
  E: U1.P2, U2.E
  DB4: U1.P4, U2.DB4
  DB5: U1.P5, U2.DB5
  DB6: U1.P6, U2.DB6
  DB7: U1.P7, U2.DB7
  V0: U2.VO, R1.wiper
  N1: U3.IP+, U4.MAIN
  N2: U3.IP-, M1.pin_2
  N3: U3.VOUT, R2.Pin_0
  N4: M1.pin_1, VCC1.-
  N5: VCC1.+, U4.NO
  N6: U4.COIL2, Q1.C, D1.anode
  N7: U5.Pin_1, R4.Pin_1
  N8: U5.Pin_3, R5.Pin_0
  N9: R5.Pin_1, Q1.B
  N10: LED1.anode, R6.Pin_1
